# Fritzing sketch PiTag (saved by Fritzing 0.9.2b)
breadboards: 1

parts:
  U1 = NodeMCU V1.0
  Part1 = RFID-RC522-v2
  LED1 = Neopixel Single LED [package="5 mm [THT]"]
  Power_plug1 = Power plug

nets:
  N1: U1.D2, Part1.SDA
  N2: U1.D3, LED1.DIN
  3V3: U1.3V3, Part1.3.3V, LED1.+5V
  GND: U1.GND, Part1.GND, LED1.GND, Power_plug1.GND
  N3: U1.D5, Part1.SCK
  N4: U1.D6, Part1.MISO
  N5: U1.D7, Part1.MOSI
  VIN: U1.Vin, Power_plug1.VCC

notes:
  >5V

custom parts:
  NodeMCU V1.0: ESP8266 based NodeMCU
  RFID-RC522-v2: A simple China made RFID-RC522 Reader; do check the pin labels, as this is a MFRC522 based clone.
  Neopixel Single LED: A 5mm neopixel through hole LED, with integrated chipset.
